// Logisim project main.circ as structural Verilog: 1 circuit, main circuit main
module main (
);

  wire and_1_out, and_2_out, and_3_out, and_4_out, clock_1_out, comparator_1_eq, counter_1_carry,
       counter_2_carry, d_ff_1_q, gpu_1_p3, gpu_1_p4, or_1_out;
  wire [1:0] counter_2_q, rom_1_data;
  wire [6:0] counter_1_q;
  wire [7:0] gpu_1_p5, gpu_1_p6, gpu_1_p7, gpu_1_p8, gpu_1_p9, gpu_1_p10, gpu_1_p11, gpu_1_p12, gpu_1_p13,
       gpu_1_p14, gpu_1_p15, gpu_1_p16, gpu_1_p17, gpu_1_p18, gpu_1_p19, gpu_1_p20;

  Clock clock_1 (.out(clock_1_out));
  Counter #(.width(7), .max('h7f), .trigger("falling")) counter_1 (
    .Q(counter_1_q), .carry(counter_1_carry), .clk(counter_2_carry));  // open: load, D, count, clr
  Counter #(.width(2), .max('h3), .trigger("falling")) counter_2 (
    .Q(counter_2_q), .carry(counter_2_carry), .clk(clock_1_out));  // open: load, D, count, clr
  Comparator #(.width(2)) comparator_1 (.a(counter_2_q), .b(2'b10), .eq(comparator_1_eq));  // open: gt, lt
  ROM #(.addrWidth(7), .dataWidth(2)) rom_1 (.addr(counter_1_q), .data(rom_1_data));  // open: sel
  and and_1 (and_1_out, counter_1_carry, comparator_1_eq);
  or or_1 (or_1_out, rom_1_data[0], rom_1_data[1]);
  and and_2 (and_2_out, or_1_out, 1'b1);
  D_Flip_Flop d_ff_1 (.clk(clock_1_out), .D(gpu_1_p4), .Q(d_ff_1_q));  // open: Qn, preset, en, reset
  and and_3 (and_3_out, d_ff_1_q, clock_1_out);
  and and_4 (and_4_out, and_2_out, clock_1_out);
  // GPU gpu_1: pin names not known; wires that end beside it: counter_1_q, d_ff_1_q, gpu_1_p3, gpu_1_p4, gpu_1_p5, gpu_1_p6, gpu_1_p7, gpu_1_p8, gpu_1_p9, gpu_1_p10, gpu_1_p11, gpu_1_p12, gpu_1_p13, gpu_1_p14, gpu_1_p15, gpu_1_p16, gpu_1_p17, gpu_1_p18, gpu_1_p19, gpu_1_p20
  or or_2 (gpu_1_p3, and_3_out, and_4_out);
  DotMatrix #(.inputtype("row"), .matrixcols(8), .matrixrows(16), .dotshape("circle")) dotmatrix_1 (
    .row0(gpu_1_p5), .row1(gpu_1_p6), .row2(gpu_1_p7), .row3(gpu_1_p8), .row4(gpu_1_p9), .row5(gpu_1_p10),
    .row6(gpu_1_p11), .row7(gpu_1_p12), .row8(gpu_1_p13), .row9(gpu_1_p14), .row10(gpu_1_p15),
    .row11(gpu_1_p16), .row12(gpu_1_p17), .row13(gpu_1_p18), .row14(gpu_1_p19), .row15(gpu_1_p20));
  T_Flip_Flop #(.trigger("falling")) t_ff_1 (
    .clk(clock_1_out), .T(and_1_out), .Q(gpu_1_p4));  // open: Qn, preset, reset, en

  // Notes on the sheet:
  //   contents of rom_1 (hex, n*v repeats v):
  //   1 126*0 1
endmodule
