// Logisim project main.circ as structural Verilog: 1 circuit, main circuit main
module main (
  output [6:0] out_1,
  output \CZY_RUCH_BYŁ_ZABLOKOWANY ,
  output FINISH_PRZESUW,
  output FINISH_ROT
);

  wire and_1_out, and_2_out, blc_rand_1_game_over, blc_rand_1_out_b, button_1_out, CLK, clock_1_out,
       comparator_1_gt, comparator_4_eq, comparator_5_eq, comparator_6_eq, comparator_7_eq, comparator_8_eq,
       controlled_buffer_1_out, d_ff_3_qn, deleting_rows_1_out_4, Deleting_Rows_CLK, demultiplexer_2_out0,
       demultiplexer_2_out1, demultiplexer_3_out0, demultiplexer_3_out1, Game_CLK, gpu_manager_1_out_6,
       gpu_manager_1_out_7, gpu_manager_1_out_8, gpu_manager_1_out_9, keyboard_1_avail,
       keyboard_manager_1_out_5, keyboard_manager_1_out_6, main_1_finish, main_1_ram_clk, main_1_zderzenie,
       main_2_ram_clk, main_2_zd, main_3_ram_clk, main_3_zd, main_4_flaga, main_4_flaga_2,
       main_4_trwajaca_akcja, not_1_out, or_1_out, or_2_out, or_3_out, or_4_out, RAM_CLK;
  wire [1:0] blc_rand_1_out_d, comparator_3_eq, Data_In, Data_Out, Deleting_Rows_Data_In,
       Deleting_Rows_Data_Out, demultiplexer_1_out2, demultiplexer_1_out4, Game_Data, Game_Data_In, Gpu_Data,
       main_1_data_out, main_2_data_out, main_3_data_out;
  wire [2:0] State_Select;
  wire [6:0] adder_1_out, Adress, blc_rand_1_out_a, Deleting_Rows_Adress, Game_Adress, GPU_Adress,
       gpu_manager_1_out_5, keyboard_1_data, keyboard_manager_1_out_4, main_1_a, main_2_a, main_2_nowe_a1,
       main_3_a, multiplexer_1_out, multiplexer_2_out;
  wire [7:0] gpu_1_p5, gpu_1_p6, gpu_1_p7, gpu_1_p8, gpu_1_p9, gpu_1_p10, gpu_1_p11, gpu_1_p12, gpu_1_p13,
       gpu_1_p14, gpu_1_p15, gpu_1_p16, gpu_1_p17, gpu_1_p18, gpu_1_p19, gpu_1_p20;

  Demultiplexer #(.select(3), .width(2)) demultiplexer_1 (
    .out1(Gpu_Data), .out2(demultiplexer_1_out2), .out3(Game_Data), .out4(demultiplexer_1_out4),
    .out5(Deleting_Rows_Data_In), .in(Data_Out), .sel(State_Select));  // open: out0, out6, out7, en
  Comparator #(.width(7), .mode("unsigned")) comparator_1 (
    .a(adder_1_out), .b(7'b1100100), .gt(comparator_1_gt));  // open: eq, lt
  Multiplexer #(.width(7), .disabled(0), .enable("false")) multiplexer_1 (
    .in0(adder_1_out), .in1(out_1), .out(multiplexer_1_out), .sel(and_1_out));
  and and_1 (and_1_out, comparator_1_gt, ~comparator_3_eq[1]);  // AND_Gate
  Comparator #(.width(3), .mode("unsigned")) comparator_2 (
    .a(State_Select), .b(3'b011), .eq(comparator_3_eq[1]));  // open: gt, lt
  Multiplexer #(.select(2), .width(7), .enable("false")) multiplexer_2 (
    .in0(multiplexer_1_out), .in1(7'b0000010), .in2(main_2_nowe_a1), .in3(main_2_nowe_a1),
    .out(multiplexer_2_out), .sel(comparator_3_eq));
  Register #(.width(7)) register_1 (.D(multiplexer_2_out), .Q(out_1), .clk(or_1_out));  // open: en, clr
  or or_1 (or_1_out, blc_rand_1_out_b, FINISH_PRZESUW, main_1_finish);
  Adder #(.width(7)) adder_1 (.a(out_1), .b(7'b0001000), .out(adder_1_out));  // open: cin, cout
  Comparator #(.width(3), .mode("unsigned")) comparator_3 (
    .a(State_Select), .b(3'b100), .eq(comparator_3_eq[0]));  // open: gt, lt
  Comparator #(.width(3), .mode("unsigned")) comparator_4 (
    .a(State_Select), .b(3'b010), .eq(comparator_4_eq));  // open: gt, lt
  Comparator #(.width(3), .mode("unsigned")) comparator_5 (
    .a(State_Select), .b(3'b101), .eq(comparator_5_eq));  // open: gt, lt
  Comparator #(.width(3), .mode("unsigned")) comparator_6 (
    .a(State_Select), .b(3'b001), .eq(comparator_6_eq));  // open: gt, lt
  Comparator #(.width(3), .mode("unsigned")) comparator_7 (
    .a(State_Select), .b(3'b001), .eq(comparator_7_eq));  // open: gt, lt
  Demultiplexer demultiplexer_2 (
    .out0(demultiplexer_2_out0), .out1(demultiplexer_2_out1), .in(CLK), .sel(main_4_trwajaca_akcja));  // open: en
  Demultiplexer demultiplexer_3 (
    .out0(demultiplexer_3_out0), .out1(demultiplexer_3_out1), .in(comparator_3_eq[1]),
    .sel(main_4_trwajaca_akcja));  // open: en
  D_Flip_Flop d_ff_1 (.clk(comparator_3_eq[0]), .D(1'b1));  // open: Q, Qn, preset, en, reset
  BLC_RAND blc_rand_1 (
    .CLK(CLK), .OUT_A(blc_rand_1_out_a), .OUT_D(blc_rand_1_out_d), .START(comparator_3_eq[0]),
    .OUT_B(blc_rand_1_out_b), .CURRENT_GAME_ADRESS(blc_rand_1_out_a),
    .CURRENT_GAME_STATE(demultiplexer_1_out4), .GAME_OVER(blc_rand_1_game_over));
  opadanie_main main_1 (
    .A1(out_1), .DATA_IN(demultiplexer_1_out2), .CLK(CLK), .ENABLE(comparator_4_eq),
    .DATA_OUT(main_1_data_out), .A(main_1_a), .RAM_CLK(main_1_ram_clk), .FINISH(main_1_finish),
    .ZDERZENIE(main_1_zderzenie), .RESET(comparator_7_eq));
  Pull_Resistor pull_resistor_1 (.node(comparator_7_eq));
  Deleting_Rows deleting_rows_1 (
    .FROM_RAM_D(Deleting_Rows_Data_In), .If_1_enables_circuit(comparator_5_eq), .CLK_input(CLK),
    .out_4(deleting_rows_1_out_4), .TO_RAM_adress(Deleting_Rows_Adress), .TO_RAM_D(Deleting_Rows_Data_Out),
    .TO_RAM_CLK(Deleting_Rows_CLK));
  Multiplexer #(.width(7)) multiplexer_3 (
    .in0(main_3_a), .in1(main_2_a), .out(Game_Adress), .sel(main_4_trwajaca_akcja));  // open: en
  Pull_Resistor pull_resistor_2 (.node(comparator_6_eq));
  Pull_Resistor pull_resistor_3 (.node(comparator_6_eq));
  D_Flip_Flop d_ff_2 (.clk(blc_rand_1_game_over), .D(1'b1));  // open: Q, Qn, preset, en, reset
  and and_2 (and_2_out, main_1_finish, main_1_zderzenie);
  not not_1 (not_1_out, and_2_out);
  przesuwanie_main main_2 (
    .A1(out_1), .CLK(demultiplexer_2_out1), .ENABLE(demultiplexer_3_out1), .DATA_IN(Game_Data),
    .FLAGA(main_4_flaga), .NOWE_A1(main_2_nowe_a1), .DATA_OUT(main_2_data_out), .RAM_CLK(main_2_ram_clk),
    .ZD(main_2_zd), .A(main_2_a), .FINISH(FINISH_PRZESUW), .RESET(comparator_6_eq));
  rotacja_main main_3 (
    .A1(out_1), .CLK(demultiplexer_2_out0), .ENABLE(demultiplexer_3_out0), .DATA_IN(Game_Data),
    .FLAGA(main_4_flaga_2), .DATA_OUT(main_3_data_out), .RAM_CLK(main_3_ram_clk), .ZD(main_3_zd),
    .A(main_3_a), .FINISH(FINISH_ROT), .RESET(comparator_6_eq));
  Multiplexer #(.select(3), .width(7)) multiplexer_4 (
    .in1(GPU_Adress), .in2(main_1_a), .in3(Game_Adress), .in4(blc_rand_1_out_a), .in5(Deleting_Rows_Adress),
    .out(Adress), .sel(State_Select));  // open: in0, in6, in7, en
  D_Flip_Flop d_ff_3 (.clk(and_2_out), .D(1'b1), .Qn(d_ff_3_qn));  // open: Q, preset, en, reset
  Button button_1 (.out(button_1_out));
  assign controlled_buffer_1_out = not_1_out ? main_1_finish : 1'bz;  // Controlled_Buffer controlled_buffer_1
  Multiplexer multiplexer_5 (
    .in0(main_3_ram_clk), .in1(main_2_ram_clk), .out(Game_CLK), .sel(main_4_trwajaca_akcja));  // open: en
  Multiplexer #(.width(2)) multiplexer_6 (
    .in0(main_3_data_out), .in1(main_2_data_out), .out(Game_Data_In), .sel(main_4_trwajaca_akcja));  // open: en
  Multiplexer #(.select(3), .width(2)) multiplexer_7 (
    .in2(main_1_data_out), .in3(Game_Data_In), .in4(blc_rand_1_out_d), .in5(Deleting_Rows_Data_Out),
    .out(Data_In), .sel(State_Select));  // open: in0, in1, in6, in7, en
  Multiplexer #(.select(3)) multiplexer_8 (
    .in2(main_1_ram_clk), .in3(Game_CLK), .in4(CLK), .in5(Deleting_Rows_CLK), .out(RAM_CLK),
    .sel(State_Select));  // open: in0, in1, in6, in7, en
  or or_2 (or_2_out, button_1_out, and_2_out);
  Keyboard keyboard_1 (
    .clr(keyboard_manager_1_out_5), .avail(keyboard_1_avail), .data(keyboard_1_data));  // open: clk, re
  Clock clock_1 (.out(clock_1_out));
  Keyboard_Manager keyboard_manager_1 (
    .out_4(keyboard_manager_1_out_4), .out_5(keyboard_manager_1_out_5), .in_2(keyboard_1_avail),
    .in_1(keyboard_1_data), .out_6(keyboard_manager_1_out_6), .in_3(or_3_out));
  or or_3 (or_3_out, FINISH_PRZESUW, FINISH_ROT);
  assign CLK = d_ff_3_qn ? clock_1_out : 1'bz;  // Controlled_Buffer controlled_buffer_2
  State_Selector state_selector_1 (
    .Keyboard__Input_Happened(keyboard_manager_1_out_6), .out_8(State_Select), .New_Block_Request(or_2_out),
    .Generating_Ended(blc_rand_1_out_b), .Falling_Ended(controlled_buffer_1_out),
    .Player_Input_Ended(or_4_out), .Render(gpu_manager_1_out_9), .Deleting_Rows_Ended(deleting_rows_1_out_4));
  Multiplexer multiplexer_9 (
    .in0(main_3_zd), .in1(main_2_zd), .out(\CZY_RUCH_BYŁ_ZABLOKOWANY ), .sel(main_4_trwajaca_akcja));  // open: en
  or or_4 (or_4_out, FINISH_ROT, FINISH_PRZESUW);
  koder_klawiatura_main main_4 (
    .wejscie_ASCI(keyboard_manager_1_out_4), .FLAGA(main_4_flaga), .FLAGA_2(main_4_flaga_2),
    .TRWAJACA_AKCJA(main_4_trwajaca_akcja));
  RAM #(.addrWidth(7), .dataWidth(2), .bus("separate")) ram_1 (
    .addr(Adress), .din(Data_In), .data(Data_Out), .clk(RAM_CLK));  // open: str, sel, ld, clr
  Comparator #(.width(3), .mode("unsigned")) comparator_8 (
    .a(State_Select), .b(3'b001), .eq(comparator_8_eq));  // open: gt, lt
  GPU_manager gpu_manager_1 (
    .in_1(Gpu_Data), .out_4(GPU_Adress), .out_5(gpu_manager_1_out_5), .out_6(gpu_manager_1_out_6),
    .out_7(gpu_manager_1_out_7), .out_8(gpu_manager_1_out_8), .out_9(gpu_manager_1_out_9),
    .ENABLE(comparator_8_eq), .in_3(CLK));
  // GPU gpu_1: pin names not known; wires that end beside it: gpu_manager_1_out_5, gpu_manager_1_out_6, gpu_manager_1_out_7, gpu_manager_1_out_8, gpu_1_p5, gpu_1_p6, gpu_1_p7, gpu_1_p8, gpu_1_p9, gpu_1_p10, gpu_1_p11, gpu_1_p12, gpu_1_p13, gpu_1_p14, gpu_1_p15, gpu_1_p16, gpu_1_p17, gpu_1_p18, gpu_1_p19, gpu_1_p20
  DotMatrix #(.inputtype("row"), .matrixcols(8), .matrixrows(16), .dotshape("circle")) dotmatrix_1 (
    .row0(gpu_1_p5), .row1(gpu_1_p6), .row2(gpu_1_p7), .row3(gpu_1_p8), .row4(gpu_1_p9), .row5(gpu_1_p10),
    .row6(gpu_1_p11), .row7(gpu_1_p12), .row8(gpu_1_p13), .row9(gpu_1_p14), .row10(gpu_1_p15),
    .row11(gpu_1_p16), .row12(gpu_1_p17), .row13(gpu_1_p18), .row14(gpu_1_p19), .row15(gpu_1_p20));

  // Notes on the sheet:
  //   CLick to start
  //   ten finisz wystepuje ale od razu sie gasi, bo resetuje tez koder i zmienia flage akcji
endmodule
